// Logisim project FSM.circ as structural Verilog: 4 circuits, main circuit main
module main (
  input  \input 
);

  wire clock_1_out, output_1_output, register_1_q, register_2_q, statebitone_1_next_s_1,
       statebitzero_1_next_s_0;

  LED led_1 (.in(register_1_q));
  LED led_2 (.in(register_2_q));
  LED led_3 (.in(\input ));
  StateBitOne statebitone_1 (
    .s_0(register_2_q), .s_1(register_1_q), .\input (\input ), .next_s_1(statebitone_1_next_s_1));
  StateBitZero statebitzero_1 (
    .s_0(register_2_q), .s_1(register_1_q), .\input (\input ), .next_s_0(statebitzero_1_next_s_0));
  \output  output_1 (.s_0(register_2_q), .s_1(register_1_q), .\input (\input ), .\output (output_1_output));
  Register #(.width(1)) register_1 (.D(statebitone_1_next_s_1), .Q(register_1_q), .clk(clock_1_out));  // open: en, clr
  Register #(.width(1)) register_2 (.D(statebitzero_1_next_s_0), .Q(register_2_q), .clk(clock_1_out));  // open: en, clr
  LED led_4 (.in(statebitone_1_next_s_1));
  Clock clock_1 (.out(clock_1_out));
  LED led_5 (.in(statebitzero_1_next_s_0));
  LED led_6 (.in(output_1_output));
endmodule

module \output  (
  input  s_0,
  input  s_1,
  input  \input ,
  output \output 
);

  wire and_1_out, and_2_out, and_3_out, not_1_out, not_2_out, not_3_out, or_1_out;

  not not_1 (not_1_out, s_0);
  not not_2 (not_2_out, s_1);
  not not_3 (not_3_out, \input );
  and and_1 (and_1_out, s_1, not_3_out);
  and and_2 (and_2_out, s_0, not_2_out, \input );
  and and_3 (and_3_out, not_1_out, or_1_out);
  or or_1 (or_1_out, and_1_out, not_2_out);
  or or_2 (\output , and_3_out, and_2_out);
endmodule

// st1
module StateBitOne (
  input  s_0,
  input  s_1,
  input  \input ,
  output next_s_1
);

  wire and_1_out, not_1_out, not_2_out;

  not not_1 (not_1_out, s_0);
  not not_2 (not_2_out, \input );
  and and_1 (and_1_out, not_1_out, not_2_out);
  not not_3 (next_s_1, and_1_out);
endmodule

// st0
module StateBitZero (
  input  s_0,
  input  s_1,
  input  \input ,
  output next_s_0
);

  wire and_1_out, not_1_out;

  not not_1 (not_1_out, s_1);
  and and_1 (and_1_out, not_1_out, \input );
  not not_2 (next_s_0, and_1_out);
endmodule
